# Fritzing sketch personal alarm (saved by Fritzing 0.9.6b)
circuit board: 8.46667cm x 5.64444cm

parts:
  Q2 = PNP-Transistor [package="TO92 [THT]"]
  R2 = Resistor [tolerance=±5% power=0.25 resistance=100 package=THT]
  C2 = Ceramic Capacitor [capacitance=100µ voltage=25V package="100 mil [THT, multilayer]"]
  SPKR1 = Loudspeaker
  S1 = SWITCH-MOMENTARY-2 [package=tactile_switch_smd-2]
  R1 = Resistor [tolerance=±5% power=0.25 resistance=330k package=THT]
  Q1 = NPN-Transistor [package="SOT-23 [SMD]"]
  VCC1 = Battery
  C1 = Ceramic Capacitor [capacitance=10nF voltage=63V package="100 mil [THT, multilayer]"]

nets:
  N1: Q2.E, C2.1, R1.Pin_0, VCC1.+
  N2: Q2.B, Q1.1
  N3: Q2.C, SPKR1.pin1, S1.1, R1.Pin_1, Q1.0, C1.0, C1.1
  N4: R2.Pin_0, Q1.2
  N5: R2.Pin_1, C2.0, SPKR1.pin2, S1.2, VCC1.-
